// Logisim project 4_bit_PC.circ as structural Verilog: 8 circuits, main circuit Data Memory
module Data_Memory (
  input  Mem_write,
  input  Mem_read,
  input  [3:0] Address,
  input  [3:0] Write_Data,
  input  Clock,
  input  Reset,
  output [3:0] Read_Data
);

  wire not_1_out;

  not not_1 (not_1_out, Clock);
  RAM #(.addrWidth(4), .dataWidth(4), .bus("separate")) ram_1 (
    .addr(Address), .din(Write_Data), .data(Read_Data), .str(Mem_write), .clk(not_1_out), .ld(Mem_read),
    .clr(Reset));  // open: sel
endmodule

module Instruction (
  input  [7:0] PC,
  output [3:0] Opcode,
  output [3:0] Instruction_8_11,
  output [3:0] Instruction_4_7,
  output [3:0] Instruction_0_3
);

  ROM #(.dataWidth(16)) rom_1 (
    .addr(PC), .data({Opcode, Instruction_8_11, Instruction_4_7, Instruction_0_3}), .sel(1'b1));

  // Notes on the sheet:
  //   ins will start from 1
  //   contents of rom_1 (hex, n*v repeats v):
  //   7513 452e 2120 5123 24 3213 b221 9231 c140 f331 e224 c120 1020 6421 8115 d241 c140 9021 c0d0
endmodule

// Pc
module PC (
  input  [7:0] PC_in,
  input  Clock,
  input  Reset,
  output [7:0] PC_out
);

  Register PC (.D(PC_in), .Q(PC_out), .clk(Clock), .clr(Reset));  // open: en
endmodule

module ALU (
  input  [2:0] ALU_op,
  input  [3:0] A,
  input  [3:0] B,
  output [3:0] Result,
  output Zero
);

  wire [3:0] adder_1_out, and_1_out, nor_1_out, or_1_out, shifter_1_out, shifter_2_out, subtractor_1_out;

  assign or_1_out = A | B;  // OR_Gate or_1, 4 bits wide
  assign nor_1_out = ~(A | B);  // NOR_Gate nor_1, 4 bits wide
  assign and_1_out = A & B;  // AND_Gate and_1, 4 bits wide
  Adder #(.width(4)) adder_1 (.a(A), .b(B), .out(adder_1_out), .cin(1'b0));  // open: cout
  Subtractor #(.width(4)) subtractor_1 (.a(A), .b(B), .out(subtractor_1_out), .bin(1'b0));  // open: bout
  Shifter #(.width(4), .shift("lr")) shifter_1 (.in(A), .\dist (B[1:0]), .out(shifter_1_out));
  Shifter #(.width(4)) shifter_2 (.in(A), .\dist (B[1:0]), .out(shifter_2_out));
  Multiplexer #(.select(3), .width(4), .enable("false")) multiplexer_1 (
    .in0(or_1_out), .in1(nor_1_out), .in2(and_1_out), .in3(adder_1_out), .in4(subtractor_1_out),
    .in5(shifter_1_out), .in6(4'b0000), .in7(shifter_2_out), .out(Result), .sel(ALU_op));
  nor nor_2 (Zero, Result[0], Result[1], Result[2], Result[3]);

  // Notes on the sheet:
  //   See shift amount 
endmodule

module Control (
  input  [3:0] opcode,
  output RegDST,
  output Jump,
  output Branch,
  output Branch_NE,
  output MemRead,
  output MemToReg,
  output MemWrite,
  output ALUSrc,
  output RegWrite,
  output [2:0] ALUOp,
  output [11:0] out_12
);

  ROM #(.addrWidth(4), .dataWidth(12)) rom_1 (
    .addr(opcode),
    .data({out_12[11], Jump, Branch, Branch_NE, MemRead, MemToReg, MemWrite, ALUSrc, out_12[3], ALUOp}),
    .sel(1'b1));

  assign {out_12[10:4], out_12[2:0]} = {Jump, Branch, Branch_NE, MemRead, MemToReg, MemWrite, ALUSrc, ALUOp};
  assign RegDST = out_12[11];
  assign RegWrite = out_12[3];

  // Notes on the sheet:
  //   contents of rom_1 (hex, n*v repeats v):
  //   809 808 80b 73 1c 80c 1a 1b 18 204 104 1d 403 80a db 1f
endmodule

module Registers (
  input  Clock,
  input  Reg_write,
  input  [3:0] Read_register_1,
  input  [3:0] Read_register_2,
  input  [3:0] Writre_register,
  input  [3:0] Write_data,
  input  Clear,
  output [3:0] \output ,
  output [3:0] output_2,
  output [3:0] Read_data_1,
  output [3:0] output_3,
  output [3:0] Read_data_2,
  output [3:0] output_4,
  output [3:0] output_5,
  output [3:0] output_6
);

  wire and_1_out, Demux_p7, Demux_p8, Demux_p9, Demux_p10, Demux_p11, Demux_p12, not_1_out;

  not not_1 (not_1_out, Clock);
  and and_1 (and_1_out, Reg_write, not_1_out);
  // _74238 Demux: pin names not known; wires that end beside it: Writre_register[0], Writre_register[1], Writre_register[2], 1'b0, 1'b0, and_1_out, Demux_p7, Demux_p8, Demux_p9, Demux_p10, Demux_p11, Demux_p12
  Register #(.width(4)) t0 (.D(Write_data), .Q(\output ), .clk(Demux_p8), .clr(Clear));  // open: en
  Register #(.width(4)) t1 (.D(Write_data), .Q(output_2), .clk(Demux_p9), .clr(Clear));  // open: en
  Register #(.width(4)) t2 (.D(Write_data), .Q(output_3), .clk(Demux_p10), .clr(Clear));  // open: en
  Register #(.width(4)) t3 (.D(Write_data), .Q(output_4), .clk(Demux_p11), .clr(Clear));  // open: en
  Register #(.width(4)) t4 (.D(Write_data), .Q(output_5), .clk(Demux_p12), .clr(Clear));  // open: en
  Register #(.width(4)) sp_111 (.D(Write_data), .Q(output_6), .clk(Demux_p7), .clr(Clear));  // open: en
  _4_input_8x1_MUX u_4_input_8x1_mux_1 (
    .t0(\output ), .t1(output_2), .t2(output_3), .t3(output_4), .t4(output_5), .sp(output_6),
    .Register(Read_register_1), .Read_data(Read_data_1));
  _4_input_8x1_MUX u_4_input_8x1_mux_2 (
    .t0(\output ), .t1(output_2), .t2(output_3), .t3(output_4), .t4(output_5), .sp(output_6),
    .Register(Read_register_2), .Read_data(Read_data_2));

  // Notes on the sheet:
  //   5th and 6th bit is zero
endmodule

// 8x1 MUX
module _4_input_8x1_MUX (
  input  [3:0] t0,
  input  [3:0] t1,
  input  [3:0] t2,
  input  [3:0] t3,
  input  [3:0] t4,
  input  [3:0] sp,
  input  [3:0] Register,
  output [3:0] Read_data
);

  // _74151 _0: pin names not known; wires that end beside it: t3[0], t2[0], t1[0], t0[0], Read_data[0], 1'b0, t4[0], 1'b0, 1'b0, sp[0], Register[0], Register[1], Register[2]
  // _74151 _2: pin names not known; wires that end beside it: t3[2], t2[2], t1[2], t0[2], Read_data[2], 1'b0, t4[2], 1'b0, 1'b0, sp[2], Register[0], Register[1], Register[2]
  // _74151 _1: pin names not known; wires that end beside it: t3[1], t2[1], t1[1], t0[1], Read_data[1], 1'b0, t4[1], 1'b0, 1'b0, sp[1], Register[0], Register[1], Register[2]
  // _74151 _3: pin names not known; wires that end beside it: t3[3], t2[3], t1[3], t0[3], Read_data[3], 1'b0, t4[3], 1'b0, 1'b0, sp[3], Register[0], Register[1], Register[2]

  // Notes on the sheet:
  //   $zero
endmodule

module Main (
  output [7:0] Result,
  output [7:0] Result_2,
  output [3:0] t4,
  output [3:0] t3,
  output [3:0] Result_3,
  output [3:0] t2,
  output [3:0] t1,
  output [3:0] t0,
  output [3:0] Data,
  output [3:0] out_10,
  output [3:0] out_11,
  output [3:0] Result_4,
  output [3:0] out_13,
  output [3:0] out_14,
  output [3:0] out_15,
  output [3:0] out_16,
  output [3:0] out_17
);

  wire alu_1_zero, Clock_out, control_1_alusrc, control_1_branch, control_1_branch_ne, control_1_jump,
       control_1_memread, control_1_memtoreg, control_1_memwrite, control_1_regdst, control_1_regwrite,
       multiplexer_3_out, Reset_out;
  wire [2:0] control_1_aluop;
  wire [3:0] Data_Memory_read_data;
  wire [7:0] adder_1_out, adder_2_out, multiplexer_2_out, pc_1_pc_out;

  Clock Clock (.out(Clock_out));
  Button Reset (.out(Reset_out));
  // Probe on Result
  // Probe on pc_1_pc_out
  PC pc_1 (.PC_in(Result), .Clock(Clock_out), .Reset(Reset_out), .PC_out(pc_1_pc_out));
  Instruction Instruction (
    .PC(pc_1_pc_out), .Opcode(out_10), .Instruction_8_11(out_11), .Instruction_4_7(out_13),
    .Instruction_0_3(out_15));
  Adder adder_1 (.a(pc_1_pc_out), .b(8'h1), .out(adder_1_out));  // open: cin, cout
  Control control_1 (
    .opcode(out_10), .RegDST(control_1_regdst), .Jump(control_1_jump), .Branch(control_1_branch),
    .Branch_NE(control_1_branch_ne), .MemRead(control_1_memread), .MemToReg(control_1_memtoreg),
    .MemWrite(control_1_memwrite), .ALUSrc(control_1_alusrc), .RegWrite(control_1_regwrite),
    .ALUOp(control_1_aluop));  // open: out_12
  assign Result_2 = {{4{out_15[3]}}, out_15};  // Bit_Extender bit_extender_1
  Multiplexer #(.width(4), .enable("false")) multiplexer_1 (
    .in0(out_13), .in1(out_15), .out(out_17), .sel(control_1_regdst));
  Adder adder_2 (.a(Result_2), .b(adder_1_out), .out(adder_2_out));  // open: cin, cout
  Registers registers_1 (
    .Read_register_1(out_11), .Read_register_2(out_13), .Writre_register(out_17), .Write_data(Result_4),
    .Reg_write(control_1_regwrite), .Clock(Clock_out), .Clear(Reset_out), .\output (t0), .output_2(t1),
    .Read_data_1(out_14), .output_3(t2), .Read_data_2(Data), .output_4(t3), .output_5(t4));  // open: output_6
  Multiplexer #(.width(8), .enable("false")) multiplexer_2 (
    .in0(adder_1_out), .in1(adder_2_out), .out(multiplexer_2_out), .sel(multiplexer_3_out));
  Multiplexer #(.enable("false")) multiplexer_3 (
    .in0(control_1_branch_ne), .in1(control_1_branch), .out(multiplexer_3_out), .sel(alu_1_zero));
  Multiplexer #(.width(4), .enable("false")) multiplexer_4 (
    .in0(Data), .in1(out_15), .out(out_16), .sel(control_1_alusrc));
  Multiplexer #(.width(8), .enable("false")) multiplexer_5 (
    .in0(multiplexer_2_out), .in1({out_11, out_13}), .out(Result), .sel(control_1_jump));
  ALU alu_1 (.ALU_op(control_1_aluop), .A(out_14), .B(out_16), .Result(Result_3), .Zero(alu_1_zero));
  Data_Memory Data_Memory (
    .Address(Result_3), .Write_Data(Data), .Clock(Clock_out), .Reset(Reset_out),
    .Mem_write(control_1_memwrite), .Mem_read(control_1_memread), .Read_Data(Data_Memory_read_data));
  Multiplexer #(.width(4), .enable("false")) multiplexer_6 (
    .in0(Result_3), .in1(Data_Memory_read_data), .out(Result_4), .sel(control_1_memtoreg));

  // Notes on the sheet:
  //   sw: src, o(dst)
  //   lw; dst, o(src)
  //   1,2,3,4
  //   op, address(dst.data), src.data, off
  //   op, address(src.data), dst off
endmodule
